# Fritzing sketch Circuit (saved by Fritzing 0.9.3b)

parts:
  Part2 = Arduino Leonardo (Rev3b)
  Part3 = HX711 Weighing Sensor Module
  S1 = Load Sensor - 50kg [part_number=SEN-10245]
  R2 = Resistor [tolerance=±2% resistance=1k package=THT]
  R1 = Resistor [tolerance=±2% resistance=1k package=THT]  # not connected
  Part4 = HX711 Weighing Sensor Module
  S2 = Load Sensor - 50kg [part_number=SEN-10245]
  R3 = Resistor [tolerance=±2% resistance=1k package=THT]
  R4 = Resistor [tolerance=±2% resistance=1k package=THT]
  Part5 = HX711 Weighing Sensor Module
  S3 = Load Sensor - 50kg [part_number=SEN-10245]
  R5 = Resistor [tolerance=±2% resistance=1k package=THT]
  R6 = Resistor [tolerance=±2% resistance=1k package=THT]
  Part6 = HX711 Weighing Sensor Module
  S4 = Load Sensor - 50kg [part_number=SEN-10245]
  R7 = Resistor [tolerance=±2% resistance=1k package=THT]
  R8 = Resistor [tolerance=±2% resistance=1k package=THT]
  Part7 = HX711 Weighing Sensor Module
  Part8 = HX711 Weighing Sensor Module
  Part9 = HX711 Weighing Sensor Module
  S5 = Load Sensor - 50kg [part_number=SEN-10245]
  S6 = Load Sensor - 50kg [part_number=SEN-10245]
  S7 = Load Sensor - 50kg [part_number=SEN-10245]
  R9 = Resistor [tolerance=±2% resistance=1k package=THT]
  R10 = Resistor [tolerance=±2% resistance=1k package=THT]
  R11 = Resistor [tolerance=±2% resistance=1k package=THT]
  R12 = Resistor [tolerance=±2% resistance=1k package=THT]
  R13 = Resistor [tolerance=±2% resistance=1k package=THT]
  R14 = Resistor [tolerance=±2% resistance=1k package=THT]  # not connected
  Part10 = HX711 Weighing Sensor Module
  S8 = Load Sensor - 50kg [part_number=SEN-10245]
  R15 = Resistor [tolerance=±2% resistance=1k package=THT]
  R16 = Resistor [tolerance=±2% resistance=1k package=THT]
  S9 = Momentary Switch [package=ksa_sealed_tac_switch]
  S10 = Momentary Switch [package=ksa_sealed_tac_switch]
  S11 = Momentary Switch [package=ksa_sealed_tac_switch]
  S12 = Momentary Switch [package=ksa_sealed_tac_switch]
  S13 = Momentary Switch [package=ksa_sealed_tac_switch]
  S14 = Momentary Switch [package=ksa_sealed_tac_switch]
  S15 = Momentary Switch [package=ksa_sealed_tac_switch]
  S16 = Momentary Switch [package=ksa_sealed_tac_switch]
  D1 = Diode [package=diode-1n4148]
  D2 = Diode [package=diode-1n4148]
  D3 = Diode [package=diode-1n4148]
  D4 = Diode [package=diode-1n4148]
  D5 = Diode [package=diode-1n4148]
  D6 = Diode [package=diode-1n4148]
  D7 = Diode [package=diode-1n4148]
  D8 = Diode [package=diode-1n4148]

nets:
  N1: Part2.D1/TX, S15.1
  N2: Part2.D2/SDA, S13.1
  N3: Part2.D3_PWM/SCL, S12.1
  N4: Part2.D4/A6, S10.1
  N5: Part2.D5_PWM, Part10.DO/RX
  N6: Part2.D6_PWM/A7, Part7.DO/RX
  N7: Part2.D7, Part9.DO/RX
  5V: Part2.5V, Part3.VCC
  GND: Part2.GND, Part3.GND
  N8: Part2.D8/A8, Part8.DO/RX
  N9: Part2.D9_PWM/A9, Part6.DO/RX
  N10: Part2.D10_PWM/A10, Part5.DO/RX
  N11: Part2.D11_PWM, Part4.DO/RX
  N12: Part2.D12/A11, Part3.DO/RX
  N13: Part2.D13_PWM, Part3.CK/TX
  N14: Part3.E+, S1.W
  N15: Part3.E-, S1.B
  N16: Part3.A+, R2.Pin_1
  N17: Part3.A-, S1.R
  N18: Part4.E+, S2.W, R3.Pin_0
  N19: Part4.E-, S2.B
  N20: Part4.A+, R4.Pin_1
  N21: Part4.A-, S2.R
  N22: Part5.E+, S3.W, R6.Pin_0
  N23: Part5.E-, S3.B
  N24: Part5.A+, R5.Pin_1
  N25: Part5.A-, S3.R
  N26: Part6.E+, S4.W, R7.Pin_0
  N27: Part6.E-, S4.B
  N28: Part6.A+, R8.Pin_1
  N29: Part6.A-, S4.R
  N30: Part7.E+, S7.W, R11.Pin_0
  N31: Part7.E-, S7.B
  N32: Part7.A+, R9.Pin_1
  N33: Part7.A-, S7.R
  N34: Part8.A+, R12.Pin_1
  N35: Part8.A-, S5.R
  N36: Part9.E+, S6.W, R13.Pin_0
  N37: Part9.E-, S6.B
  N38: Part9.A+, R10.Pin_1
  N39: Part9.A-, S6.R
  N40: Part10.E+, S8.W, R16.Pin_0
  N41: Part10.E-, S8.B
  N42: Part10.A+, R15.Pin_1
  N43: Part10.A-, S8.R
  N44: S9.1, D1.C, D2.C
  N45: S11.1, D3.C, D4.C
  N46: S14.1, D7.C, D8.C
  N47: S16.1, D5.C, D6.C

custom parts:
  Load Sensor - 50kg: Half-wheatstone bridge Load Cell modified from the Fritzing Repo This load sensor, sometimes called a strain gauge, is the same one found in digital bathroom scales (you know, the ones you use in January for your New Year's resolutions, and then forget about a month later). This sensor can measure up to about 110 pounds.
